# Fritzing sketch TurnItDownANotch (saved by Fritzing 0.9.3b)
breadboards: 1

parts:
  R1 = Rotary Potentiometer (Small) [maximum_resistance=100kΩ package=THT]
  Onderdeel1 = Arduino Uno (Rev3)
  R2 = Resistor [tolerance=±5% resistance=220 package="2010 [SMD]"]

nets:
  N1: R1.leg1, Onderdeel1.GND, R2.Pin_1
  N2: R1.wiper, Onderdeel1.A0, R2.Pin_0
  N3: R1.leg2, Onderdeel1.5V
